# Fritzing sketch 9.10 Fritzing Test (saved by Fritzing 0.9.5d)
breadboards: 1

parts:
  Part1 = Arduino Nano 33 IOT
  LED1 = LED - 5mm [color="Red (633nm)" package="5 mm [THT]"]
  R1 = Resistor [tolerance=±5% resistance=220 package="0603 [SMD]"]
  S1 = Pushbutton [package="[SMD]"]

nets:
  N1: Part1.RESET, Part1.A7
  N2: Part1.GND, Part1.D13~, S1.Pin_3, S1.Pin_4
  N3: Part1.D11/MOSI, Part1.+5V
  N4: Part1.3V3, R1.Pin_1
  N5: LED1.cathode, S1.Pin_1, S1.Pin_2
  N6: LED1.anode, R1.Pin_0

custom parts:
  Arduino Nano 33 IOT: The Arduino Nano 33 IoT is the easiest and cheapest point of entry to enhance existing devices (and creating new ones) to be part of the IoT and designing pico-network applications. Whether you are looking at building a sensor network connected to your office or home router, or if you want to create a BLE device sending data to a cellphone, the Nano 33 IoT is your one-stop-solution for many of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
