# Fritzing sketch hall-effect-test (saved by Fritzing 0.9.5d)
breadboards: 1

parts:
  M1 = MKR ZERO
  S1 = Toggle Switch [package=THT]
  R1 = Resistor [tolerance=±5% resistance=220 package="0402 [SMD]"]
  LED1 = smd LED [color="Red (633nm)" package="1206 [SMD]"]
  R2 = Resistor [tolerance=±5% resistance=220 package="0402 [SMD]"]

nets:
  N1: M1.D0, R2.Pin_1
  N2: M1.D6, S1.L1, R1.Pin_1
  N3: M1.GND, M1.-VBAT, S1.COM, LED1.cathode
  5V: M1.5V, M1.+5V, S1.L2, R1.Pin_0
  N4: M1.SCL, M1.SDA
  N5: LED1.anode, R2.Pin_0

custom parts:
  MKR ZERO: arduino mrk zero SAMD21 Cortex-M0+ 32bit low power ARM MCU 256 meg flash 32kb sram 48mhz
